// Logisim project project2.circ as structural Verilog: 1 circuit, main circuit main
module main (
);

  wire and_1_out, and_2_out, and_3_out, and_4_out, clock_1_out, clock_2_out, decoder_1_out0, decoder_1_out1,
       decoder_1_out2, decoder_1_out3;
  wire [7:0] adder_1_out, adder_2_out, DataMemory_dout, InstructionMemory_dout, multiplexer_1_out,
       multiplexer_2_out, multiplexer_3_out, multiplexer_4_out, PC_q, reg0_q, reg1_q, reg2_q, reg3_q,
       subtractor_1_out;

  Clock clock_1 (.out(clock_1_out));
  Adder adder_1 (.a(PC_q), .b(8'h1), .out(adder_1_out));  // open: cin, cout
  RAM #(.enables("line")) InstructionMemory (
    .addr(PC_q), .we(1'b0), .clk(clock_1_out), .dout(InstructionMemory_dout));  // open: din
  Register PC (.D(adder_1_out), .en(1'b1), .clk(clock_1_out), .Q(PC_q));  // open: clr
  Clock clock_2 (.out(clock_2_out));
  Decoder #(.select(2)) decoder_1 (
    .out0(decoder_1_out0), .out1(decoder_1_out1), .out2(decoder_1_out2), .out3(decoder_1_out3),
    .sel(InstructionMemory_dout[3:2]), .en(1'b1));
  RAM DataMemory (
    .addr(multiplexer_4_out), .we(1'b0), .oe(1'b1), .clk(clock_2_out), .dout(DataMemory_dout));  // open: din
  and and_1 (and_1_out, 1'b1, decoder_1_out0);
  and and_2 (and_2_out, 1'b1, decoder_1_out1);
  and and_3 (and_3_out, 1'b1, decoder_1_out2);
  and and_4 (and_4_out, 1'b1, decoder_1_out3);
  Multiplexer #(.width(8)) multiplexer_1 (
    .in0(multiplexer_4_out), .in1(DataMemory_dout), .out(multiplexer_1_out), .sel(InstructionMemory_dout[0]));
  Register reg0 (.D(multiplexer_1_out), .en(and_1_out), .clk(clock_1_out), .Q(reg0_q));  // open: clr
  Register reg1 (.D(multiplexer_1_out), .en(and_2_out), .clk(clock_1_out), .Q(reg1_q));  // open: clr
  Register reg2 (.D(multiplexer_1_out), .en(and_3_out), .clk(clock_1_out), .Q(reg2_q));  // open: clr
  Register reg3 (.D(multiplexer_1_out), .en(and_4_out), .clk(clock_1_out), .Q(reg3_q));  // open: clr
  Multiplexer #(.select(2), .width(8)) multiplexer_2 (
    .in0(reg0_q), .in1(reg1_q), .in2(reg2_q), .in3(reg3_q), .out(multiplexer_2_out),
    .sel(InstructionMemory_dout[5:4]));
  Multiplexer #(.select(2), .width(8)) multiplexer_3 (
    .in0(reg0_q), .in1(reg1_q), .in2(reg2_q), .in3(reg3_q), .out(multiplexer_3_out),
    .sel(InstructionMemory_dout[7:6]));
  Adder adder_2 (.a(multiplexer_2_out), .b(multiplexer_3_out), .out(adder_2_out));  // open: cin, cout
  Subtractor subtractor_1 (.a(multiplexer_2_out), .b(multiplexer_3_out), .out(subtractor_1_out));  // open: bin, bout
  Multiplexer #(.width(8)) multiplexer_4 (
    .in0(adder_2_out), .in1(subtractor_1_out), .out(multiplexer_4_out), .sel(InstructionMemory_dout[1]));

  // Notes on the sheet:
  //   Elizabeth Bruski
  //   I pledge my honor that I have abided by the Stevens Honor System.
  //   control unit
  //   WriteReg
  //   regwrite
  //   0 bit: opcode control: 1 for load, 0 for arithmetic
  //   RegDataW
  //   ReadReg1
  //   ReadReg2
  //   RegData1
  //   RegData2
  //   ALUout
endmodule
